# Fritzing sketch AARR_ServoBot-BB (saved by Fritzing 0.9.2b)
breadboards: 1

parts:
  Part1 = Arduino Pro Mini v13
  Part2 = Breakout Board for Electret Microphone
  U1 = LIPO-1000mAh [package=lipo-1000]
  S3 = Pushbutton [package="[THT]"]
  R1 = Rotary Potentiometer (Small) [maximum_resistance=10kΩ package=THT]
  R2 = Rotary Potentiometer (Small) [maximum_resistance=10kΩ package=THT]
  R3 = Rotary Potentiometer (Small) [maximum_resistance=10kΩ package=THT]
  LED1 = RGB LED (com. cathode, rgb) [package="5 mm [THT]"]
  D1 = Schottky Diode [part_number=1N5817 package="300 mil [THT]"]
  R5 = Resistor [tolerance=±5% resistance=100 package=THT]
  R6 = Resistor [tolerance=±5% resistance=180 package=THT]
  R7 = Resistor [tolerance=±5% resistance=100 package=THT]
  S6 = Toggle Switch [package=THT]
  R9 = Resistor [tolerance=±5% resistance=10k package=THT]
  J1 = Basic Servo

nets:
  GND: Part1.GND, Part2.GND, U1.-, R1.leg1, R2.leg1, R3.leg1, LED1.common_cathode, R9.Pin_1, J1.gnd
  N1: Part1.RAW, D1.anode, S6.COM
  VCC: Part1.VCC, Part2.VCC, S3.Pin_1, S3.Pin_2, R1.leg2, R2.leg2, R3.leg2
  N2: Part1.A3, Part2.AUD
  N3: Part1.A2, R1.wiper
  N4: Part1.A1, R2.wiper
  N5: Part1.A0, R3.wiper
  N6: Part1.D11_PWM/MOSI, R5.Pin_1
  N7: Part1.D9_PWM, J1.pulse
  N8: Part1.D5_PWM, R7.Pin_1
  N9: Part1.D3_PWM, R6.Pin_1
  N10: Part1.D2, S3.Pin_3, S3.Pin_4, R9.Pin_0
  N11: U1.+, S6.L2
  N12: LED1.red_anode, R6.Pin_0
  N13: LED1.green_anode, R7.Pin_0
  N14: LED1.blue_anode, R5.Pin_0
  N15: D1.cathode, J1.vcc
